# Fritzing sketch Tumbglove (saved by Fritzing 0.7.11b)
breadboards: 1

parts:
  Arduino1 = Arduino
  R2 = Resistor [tolerance=±5% resistance=10k package=THT]
  R1 = Basic Flex Resistor

nets:
  N1: Arduino1.GND, Arduino1.A0, R2.Pin_0, R2.Pin_1, R1.pin_1
  N2: Arduino1.+5V, R1.Pin_2

notes:
  ARDUINO
  LEONARDO
